# Fritzing sketch Diagrama (saved by Fritzing 0.9.3b)
breadboards: 1

parts:
  Componente1 = Rotoshield - Motor driver shield for Arduino
  Componente2 = Arduino Uno (Rev3) - ICSP
  M1 = DC Motor
  M2 = DC Motor
  M3 = DC Motor
  M4 = DC Motor
  J1 = Basic Servo
  hc-sr1 = hc-sr04
  R1 = Resistor [tolerance=±5% resistance=220 package=THT]
  R2 = Resistor [tolerance=±5% resistance=220 package=THT]
  R3 = Resistor [tolerance=±5% resistance=220 package=THT]
  R4 = Resistor [tolerance=±5% resistance=220 package=THT]
  R5 = Resistor [tolerance=±5% resistance=220 package=THT]
  R6 = Resistor [tolerance=±5% resistance=220 package=THT]
  LED1 = LED - 3mm [color="Red (633nm)" package="3 mm [THT]"]
  LED2 = LED - 3mm [color="Green (555nm)" package="3 mm [THT]"]
  LED3 = LED - 3mm [color="Red (633nm)" package="3 mm [THT]"]
  LED4 = LED - 3mm [color="Green (555nm)" package="3 mm [THT]"]
  LED5 = LED - 3mm [color="Red (633nm)" package="3 mm [THT]"]
  LED6 = LED - 3mm [color="Green (555nm)" package="3 mm [THT]"]

nets:
  N1: Componente1.DIG_3, Componente2.D3_PWM
  N2: Componente1.DIG_4, Componente2.D4
  N3: Componente1.DIG_5, Componente2.D5_PWM
  N4: Componente1.DIG_6, Componente2.D6_PWM
  N5: Componente1.DIG_7, Componente2.D7
  N6: Componente1.DIG_8, Componente2.D8
  N7: Componente1.DIG_11, Componente2.D11_PWM/MOSI
  N8: Componente1.DIG_12, Componente2.D12/MISO
  N9: Componente1.DIG_13, Componente2.D13/SCK
  N10: Componente1.M1-2, M3.pin_2
  N11: Componente1.M1-1, M3.pin_1
  N12: Componente1.M2-2, M4.pin_2
  N13: Componente1.M2-1, M4.pin_1
  N14: Componente1.M3-2, M1.pin_2
  N15: Componente1.M3-1, M1.pin_1
  N16: Componente1.M4-2, M2.pin_2
  N17: Componente1.M4-1, M2.pin_1
  N18: Componente2.A0, R1.Pin_1
  N19: Componente2.A1, R2.Pin_1
  N20: Componente2.A2, R3.Pin_1
  N21: Componente2.A3, R4.Pin_1
  N22: Componente2.A4/SDA, R6.Pin_1
  N23: Componente2.A5/SCL, R5.Pin_1
  GND: Componente2.D9_PWM, Componente2.GND, J1.gnd, hc-sr1.Echo, hc-sr1.GND, LED1.cathode, LED2.cathode, LED3.cathode, LED4.cathode, LED5.cathode, LED6.cathode
  N24: Componente2.D10_PWM/SS, J1.pulse
  N25: Componente2.D2, hc-sr1.Trig
  VCC: Componente2.5V, J1.vcc, hc-sr1.VCC
  N26: R1.Pin_0, LED1.anode
  N27: R2.Pin_0, LED2.anode
  N28: R3.Pin_0, LED3.anode
  N29: R4.Pin_0, LED6.anode
  N30: R5.Pin_0, LED4.anode
  N31: R6.Pin_0, LED5.anode
